// Logisim project ContatoreMod60.circ as structural Verilog: 1 circuit, main circuit main
module main (
  input  [5:0] input_loaded,
  input  load,
  input  load_2,
  input  reset,
  input  in_5,
  output fullCount
);

  wire and_1_out, clock_1_out, or_1_out, t_ff_1_q, t_ff_2_q, t_ff_3_q, t_ff_4_q, t_ff_5_q, t_ff_6_q;

  Clock clock_1 (.out(clock_1_out));
  or or_1 (or_1_out, in_5, and_1_out);
  T_Flip_Flop #(.trigger("falling")) t_ff_1 (
    .clk(clock_1_out), .T(load_2), .Q(t_ff_1_q), .reset(or_1_out));  // open: Qn, preset, en
  T_Flip_Flop #(.trigger("falling")) t_ff_2 (
    .clk(t_ff_1_q), .T(load_2), .Q(t_ff_2_q), .reset(or_1_out));  // open: Qn, preset, en
  T_Flip_Flop #(.trigger("falling")) t_ff_3 (
    .clk(t_ff_2_q), .T(load_2), .Q(t_ff_3_q), .reset(or_1_out));  // open: Qn, preset, en
  T_Flip_Flop #(.trigger("falling")) t_ff_4 (
    .clk(t_ff_3_q), .T(load_2), .Q(t_ff_4_q), .reset(or_1_out));  // open: Qn, preset, en
  T_Flip_Flop #(.trigger("falling")) t_ff_5 (
    .clk(t_ff_4_q), .T(load_2), .Q(t_ff_5_q), .reset(or_1_out));  // open: Qn, preset, en
  and and_1 (and_1_out, ~t_ff_1_q, ~t_ff_2_q, t_ff_3_q, t_ff_4_q, t_ff_5_q, t_ff_6_q, ~clock_1_out);  // AND_Gate
  T_Flip_Flop #(.trigger("falling")) t_ff_6 (
    .clk(t_ff_5_q), .T(load_2), .Q(t_ff_6_q), .reset(or_1_out));  // open: Qn, preset, en
  nand nand_1 (fullCount, t_ff_1_q, t_ff_2_q, ~t_ff_3_q, t_ff_4_q, t_ff_5_q, t_ff_6_q, clock_1_out);  // NAND_Gate

  // Notes on the sheet:
  //   0
  //   1
  //   2
  //   3
  //   4
  //   reset_from_count
  //   Posto a 1 al 60° conteggio e con clock basso
  //   5
  //   Posto a 0 al 59° conteggio e con clock alto
endmodule
