// Logisim project Cronometro.circ as structural Verilog: 1 circuit, main circuit main
module main (
  input  load,
  input  reset,
  input  [5:0] sec_loaded,
  input  [5:0] min_loaded,
  input  [4:0] hour_loaded,
  output [5:0] sec,
  output [5:0] min,
  output [4:0] hour
);

  wire clock_1_out, counter_1_carry, counter_2_carry;

  Clock clock_1 (.out(clock_1_out));
  Counter #(.width(6), .max('h3c), .trigger("falling")) counter_1 (
    .load(load), .D(sec_loaded), .Q(sec), .carry(counter_1_carry), .clk(clock_1_out), .clr(reset));  // open: count
  Counter #(.width(6), .max('h3c), .trigger("falling")) counter_2 (
    .load(load), .D(min_loaded), .Q(min), .carry(counter_2_carry), .clk(counter_1_carry), .clr(reset));  // open: count
  Counter #(.width(5), .max('h17), .trigger("falling")) counter_3 (
    .load(load), .D(hour_loaded), .Q(hour), .clk(counter_2_carry), .clr(reset));  // open: count, carry

  // Notes on the sheet:
  //   input_loaded
  //   sec
  //   min
  //   hour
endmodule
