// Logisim project ShiftRegister.circ as structural Verilog: 1 circuit, main circuit main
module main (
  input  external_zero,
  input  external_zero_2,
  input  [3:0] in_3,
  input  external_zero_3,
  input  enable_input,
  input  enable_output,
  input  _3,
  input  _2,
  input  _1,
  input  _0,
  input  [1:0] selection,
  output [3:0] data_out
);

  wire clock_1_out, multiplexer_1_out, multiplexer_2_out, multiplexer_3_out, multiplexer_4_out,
       multiplexer_5_out, multiplexer_6_out, multiplexer_7_out, multiplexer_8_out;
  wire [3:0] d_ff_4_q;

  Clock clock_1 (.out(clock_1_out));
  Multiplexer #(.select(2)) multiplexer_1 (
    .in0(d_ff_4_q[2]), .in1(d_ff_4_q[1]), .in2(external_zero_2), .in3(external_zero_2),
    .out(multiplexer_1_out), .sel(selection));  // open: en
  Multiplexer multiplexer_2 (
    .in0(multiplexer_1_out), .in1(_3), .out(multiplexer_2_out), .sel(enable_input));  // open: en
  D_Flip_Flop d_ff_1 (.clk(clock_1_out), .D(multiplexer_2_out), .Q(d_ff_4_q[3]));  // open: Qn, preset, en, reset
  Multiplexer #(.select(2)) multiplexer_3 (
    .in0(d_ff_4_q[1]), .in1(d_ff_4_q[0]), .in2(d_ff_4_q[3]), .in3(external_zero_3), .out(multiplexer_3_out),
    .sel(selection));  // open: en
  Multiplexer multiplexer_4 (
    .in0(multiplexer_3_out), .in1(_2), .out(multiplexer_4_out), .sel(enable_input));  // open: en
  D_Flip_Flop d_ff_2 (.clk(clock_1_out), .D(multiplexer_4_out), .Q(d_ff_4_q[2]));  // open: Qn, preset, en, reset
  Multiplexer #(.select(2)) multiplexer_5 (
    .in0(d_ff_4_q[0]), .in1(external_zero), .in2(d_ff_4_q[2]), .in3(d_ff_4_q[3]), .out(multiplexer_5_out),
    .sel(selection));  // open: en
  Multiplexer multiplexer_6 (
    .in0(multiplexer_5_out), .in1(_1), .out(multiplexer_6_out), .sel(enable_input));  // open: en
  D_Flip_Flop d_ff_3 (.clk(clock_1_out), .D(multiplexer_6_out), .Q(d_ff_4_q[1]));  // open: Qn, preset, en, reset
  Multiplexer #(.select(2)) multiplexer_7 (
    .in0(external_zero), .in1(external_zero), .in2(d_ff_4_q[1]), .in3(d_ff_4_q[2]), .out(multiplexer_7_out),
    .sel(selection));  // open: en
  Multiplexer multiplexer_8 (
    .in0(multiplexer_7_out), .in1(_0), .out(multiplexer_8_out), .sel(enable_input));  // open: en
  D_Flip_Flop d_ff_4 (.clk(clock_1_out), .D(multiplexer_8_out), .Q(d_ff_4_q[0]));  // open: Qn, preset, en, reset
  Multiplexer #(.width(4)) multiplexer_9 (.in0(in_3), .in1(d_ff_4_q), .out(data_out), .sel(enable_output));  // open: en

  // Notes on the sheet:
  //   data_in
  //   1 bit a sinistra 
  //   3
  //   N.B: LE LABEL SONO SOPRA LE INTERCONNESSIONI DI RIFERIMENTO
  //   3
  //   1 bit a sinistra 
  //   2
  //   2
  //   2 bit a destra
  //   2 bit a sinistra 
  //   1 bit a sinistra 
  //   1
  //   2 bit a sinistra 
  //   1
  //   2 bit a destra
  //   2 bit a sinistra
  //   1/2 bit a sinistra 
  //   0
  //   0
endmodule
